// Logisim project File_1.circ as structural Verilog: 7 circuits, main circuit main
module main (
  input  in_1,
  output out_2,
  output out_3,
  output out_4
);

  wire clock_1_out, nand_1_out, nand_2_out, not_1_out;

  Clock clock_1 (.out(clock_1_out));
  not not_1 (not_1_out, in_1);
  nand nand_1 (nand_1_out, in_1, clock_1_out);
  nand nand_2 (nand_2_out, clock_1_out, not_1_out);
  D_Flip_Flop d_ff_1 (.clk(clock_1_out), .D(in_1), .Q(out_4));  // open: Qn, preset, en, reset
  nand nand_3 (out_2, nand_1_out, out_3);
  nand nand_4 (out_3, out_2, nand_2_out);

  // Notes on the sheet:
  //   D Latch -Can change the Output during the level 1
  //   D FLIP FLOP - Output is changed only from the transition of 0 to 1 and have to wait for next 0 to 1 to change the output
endmodule

module JK_FF_RACING (
  input  in_1,
  input  in_2,
  input  in_3,
  input  in_4,
  input  in_5,
  input  in_6,
  output out_7,
  output out_8,
  output out_9,
  output out_10,
  output out_11,
  output out_12
);

  wire clock_1_out, clock_2_out, clock_3_out, not_1_out;

  Clock clock_1 (.out(clock_1_out));
  J_K_Flip_Flop j_k_ff_1 (.J(in_2), .clk(clock_1_out), .K(in_2), .Q(out_8), .Qn(out_10));  // open: preset, en, reset
  J_K_Flip_Flop j_k_ff_2 (.J(in_4), .clk(clock_1_out), .K(in_5), .Q(out_12));  // open: Qn, preset, en, reset
  Clock clock_2 (.out(clock_2_out));
  Clock clock_3 (.out(clock_3_out));
  not not_1 (not_1_out, in_1);
  J_K_Flip_Flop j_k_ff_3 (.J(in_3), .clk(clock_2_out), .K(in_6), .Q(out_11));  // open: Qn, preset, en, reset
  J_K_Flip_Flop j_k_ff_4 (
    .J(in_1), .clk(clock_3_out), .K(not_1_out), .Q(out_7), .Qn(out_9));  // open: preset, en, reset

  // Notes on the sheet:
  //   JK ff in logisim by default are edge triggered..so only toggling happens which can be controlled by changing the inputs to J and K
  //   but in logicly ..race around condition is there which cannot be stopped (the circuit gets corrputed) even by changing the J and L inputs
endmodule

module JK_FF (
  input  in_1,
  input  in_2,
  input  in_3,
  input  in_4,
  input  in_5,
  output out_6,
  output out_7,
  output out_8,
  output out_9,
  output out_10
);

  wire clock_1_out, clock_2_out, clock_3_out, nand_1_out, nand_2_out, not_1_out;

  Clock clock_1 (.out(clock_1_out));
  Clock clock_2 (.out(clock_2_out));
  J_K_Flip_Flop j_k_ff_1 (.J(in_4), .clk(clock_2_out), .K(in_5), .Q(out_10));  // open: Qn, preset, en, reset
  J_K_Flip_Flop j_k_ff_2 (.J(in_2), .clk(clock_1_out), .K(in_3), .Q(out_7), .Qn(out_8));  // open: preset, en, reset
  Clock clock_3 (.out(clock_3_out));
  not not_1 (not_1_out, in_1);
  nand nand_1 (nand_1_out, in_1, clock_3_out, out_9);
  nand nand_2 (nand_2_out, out_6, clock_3_out, not_1_out);
  nand nand_3 (out_6, nand_1_out, out_9);
  nand nand_4 (out_9, out_6, nand_2_out);
endmodule

module master_slave_D (
  input  in_1,
  input  in_2,
  output out_3
);

  wire clock_1_out, d_latch_1_q, not_1_out;

  Clock clock_1 (.out(clock_1_out));
  d_latch d_latch_1 (.Pre(in_1), .D(in_2), .CLK(clock_1_out), .Q(d_latch_1_q));  // open: Q_prime
  not not_1 (not_1_out, clock_1_out);
  d_latch d_latch_2 (.Pre(in_1), .D(d_latch_1_q), .CLK(not_1_out), .Q(out_3));  // open: Q_prime
endmodule

module d_latch (
  input  Pre,
  input  D,
  input  CLK,
  output Q,
  output Q_prime
);

  wire nand_1_out, nand_2_out, not_1_out;

  not not_1 (not_1_out, D);
  nand nand_1 (nand_1_out, D, CLK, Q_prime);
  nand nand_2 (nand_2_out, not_1_out, CLK, Q);
  nand nand_3 (Q, nand_1_out, Pre, Q_prime);
  nand nand_4 (Q_prime, nand_2_out, Q);
endmodule

module jk_latch (
  input  PRE,
  input  J,
  input  CLK,
  input  K,
  output Q,
  output Q_prime
);

  wire nand_1_out, nand_2_out;

  nand nand_1 (nand_1_out, J, CLK, Q_prime);
  nand nand_2 (nand_2_out, Q, CLK, K);
  nand nand_3 (Q, nand_1_out, PRE, Q_prime);
  nand nand_4 (Q_prime, Q, nand_2_out);
endmodule

module MASTER_SLAVE_JK (
  input  in_1,
  input  in_2,
  input  in_3,
  input  in_4,
  input  in_5,
  input  in_6,
  input  in_7,
  output out_8,
  output out_9,
  output out_10,
  output out_11
);

  wire clock_1_out, clock_2_out, jk_latch_1_q, jk_latch_1_q_prime, nand_1_out, nand_2_out, nand_3_out,
       nand_4_out, nand_5_out, nand_6_out, not_1_out, not_2_out;

  Clock clock_1 (.out(clock_1_out));
  Clock clock_2 (.out(clock_2_out));
  jk_latch jk_latch_1 (
    .PRE(in_1), .J(in_3), .CLK(clock_1_out), .K(in_4), .Q(jk_latch_1_q), .Q_prime(jk_latch_1_q_prime));
  not not_1 (not_1_out, clock_1_out);
  nand nand_1 (nand_1_out, in_6, clock_2_out, out_11);
  nand nand_2 (nand_2_out, out_10, clock_2_out, in_7);
  jk_latch jk_latch_2 (
    .PRE(in_2), .J(jk_latch_1_q), .CLK(not_1_out), .K(jk_latch_1_q_prime), .Q(out_8), .Q_prime(out_9));
  not not_2 (not_2_out, clock_2_out);
  nand nand_3 (nand_3_out, nand_1_out, in_5, nand_4_out);
  nand nand_4 (nand_4_out, nand_3_out, nand_2_out);
  nand nand_5 (nand_5_out, nand_3_out, not_2_out);
  nand nand_6 (nand_6_out, not_2_out, nand_4_out);
  nand nand_7 (out_10, nand_5_out, out_11);
  nand nand_8 (out_11, out_10, nand_6_out);

  // Notes on the sheet:
  //   wrong model of master slave ff
  //   correct 
endmodule
