// Logisim project File_2.circ as structural Verilog
module main (
  input  M,
  output out_2,
  output out_3,
  output out_4
);

  wire clock_1_out, multiplexer_1_out, multiplexer_2_out, t_ff_1_qn, t_ff_2_qn;

  Clock clock_1 (.out(clock_1_out));
  T_Flip_Flop t_ff_1 (.clk(clock_1_out), .T(1'b1), .Q(out_4), .Qn(t_ff_1_qn));  // open: preset, reset, en
  Multiplexer multiplexer_1 (.in0(out_4), .in1(t_ff_1_qn), .out(multiplexer_1_out), .sel(M), .en(1'b1));
  T_Flip_Flop t_ff_2 (.clk(multiplexer_1_out), .T(1'b1), .Q(out_3), .Qn(t_ff_2_qn));  // open: preset, reset, en
  Multiplexer multiplexer_2 (.in0(out_3), .in1(t_ff_2_qn), .out(multiplexer_2_out), .sel(M), .en(1'b1));
  T_Flip_Flop t_ff_3 (.clk(multiplexer_2_out), .T(1'b1), .Q(out_2));  // open: Qn, preset, reset, en
endmodule

module up_and_down_counting (
  input  M,
  output out_2,
  output out_3,
  output out_4
);

  wire and_1_out, and_2_out, and_3_out, and_4_out, clock_1_out, not_1_out, or_1_out, or_2_out, t_ff_1_qn,
       t_ff_2_qn;

  Clock clock_1 (.out(clock_1_out));
  not not_1 (not_1_out, M);
  T_Flip_Flop #(.trigger("falling")) t_ff_1 (
    .clk(clock_1_out), .T(1'b1), .Q(out_4), .Qn(t_ff_1_qn));  // open: preset, reset, en
  and and_1 (and_1_out, M, t_ff_1_qn);
  and and_2 (and_2_out, not_1_out, out_4);
  T_Flip_Flop #(.trigger("falling")) t_ff_2 (
    .clk(or_1_out), .T(1'b1), .Q(out_3), .Qn(t_ff_2_qn));  // open: preset, reset, en
  or or_1 (or_1_out, and_1_out, and_2_out);
  and and_3 (and_3_out, M, t_ff_2_qn);
  and and_4 (and_4_out, not_1_out, out_3);
  T_Flip_Flop #(.trigger("falling")) t_ff_3 (.clk(or_2_out), .T(1'b1), .Q(out_2));  // open: Qn, preset, reset, en
  or or_2 (or_2_out, and_3_out, and_4_out);
endmodule

module mod_6_counter (
  output out_1,
  output out_2,
  output out_3,
  output out_4,
  output out_5
);

  wire and_1_out, clock_1_out, clock_2_out, j_k_ff_1_qn, j_k_ff_2_qn, not_1_out, not_2_out, not_3_out,
       not_4_out;

  Clock clock_1 (.out(clock_1_out));
  not not_1 (not_1_out, out_4);
  J_K_Flip_Flop #(.trigger("falling")) j_k_ff_1 (
    .J(1'b1), .clk(clock_1_out), .K(1'b1), .Q(out_3), .Qn(j_k_ff_1_qn));  // open: preset, en, reset
  D_Flip_Flop d_ff_1 (.clk(clock_1_out), .D(not_1_out), .Q(out_4));  // open: Qn, preset, en, reset
  J_K_Flip_Flop #(.trigger("falling")) j_k_ff_2 (
    .J(1'b1), .clk(j_k_ff_1_qn), .K(1'b1), .Q(out_2), .Qn(j_k_ff_2_qn));  // open: preset, en, reset
  not not_2 (not_2_out, out_5);
  J_K_Flip_Flop #(.trigger("falling")) j_k_ff_3 (
    .J(1'b1), .clk(j_k_ff_2_qn), .K(1'b1), .Q(out_1));  // open: Qn, preset, en, reset
  Clock clock_2 (.out(clock_2_out));
  not not_3 (not_3_out, not_2_out);
  S_R_Flip_Flop s_r_ff_1 (.S(not_2_out), .clk(clock_2_out), .R(not_3_out), .Q(out_5));  // open: Qn, preset, reset, en
  and and_1 (and_1_out, out_1, out_2, not_4_out);
  not not_4 (not_4_out, out_3);
endmodule

module synch_counter (
  input  in_1,
  output out_2,
  output out_3,
  output out_4,
  output out_5
);

  wire clock_1_out;

  Clock clock_1 (.out(clock_1_out));
  J_K_Flip_Flop #(.trigger("falling")) j_k_ff_1 (
    .J(out_3), .clk(clock_1_out), .K(out_3), .Q(out_2), .Qn(out_4));  // open: preset, en, reset
  J_K_Flip_Flop #(.trigger("falling")) j_k_ff_2 (
    .J(1'b1), .clk(clock_1_out), .K(1'b1), .Q(out_3), .Qn(out_5));  // open: preset, en, reset
  Clock clock_2 ();  // open: out
  D_Flip_Flop d_ff_1 (.preset(in_1));  // open: clk, D, Q, Qn, en, reset
  D_Flip_Flop d_ff_2 (.reset(in_1));  // open: clk, D, Q, Qn, preset, en
  D_Flip_Flop d_ff_3 ();  // open: clk, D, Q, Qn, preset, en, reset
  D_Flip_Flop d_ff_4 ();  // open: clk, D, Q, Qn, preset, en, reset
endmodule

module d_ff (
  input  in_1,
  input  in_2,
  output out_3,
  output out_4
);

  wire clock_1_out, nand_1_out, nand_2_out, nand_3_out, nand_4_out;

  Clock clock_1 (.out(clock_1_out));
  nand nand_1 (nand_1_out, nand_4_out, nand_2_out);
  nand nand_2 (nand_2_out, nand_1_out, clock_1_out, in_2);
  nand nand_3 (nand_3_out, nand_2_out, clock_1_out, nand_4_out);
  nand nand_4 (nand_4_out, nand_3_out, in_1, in_2);
  nand nand_5 (out_3, out_4, nand_2_out);
  nand nand_6 (out_4, nand_3_out, in_2, out_3);
endmodule

module bcd_counter (
  output out_1,
  output out_2,
  output out_3,
  output out_4
);

  wire and_1_out, clock_1_out, j_k_ff_4_qn;

  Clock clock_1 (.out(clock_1_out));
  and and_1 (and_1_out, out_3, out_2);
  J_K_Flip_Flop #(.trigger("falling")) j_k_ff_1 (
    .J(1'b1), .clk(clock_1_out), .K(1'b1), .Q(out_4));  // open: Qn, preset, en, reset
  J_K_Flip_Flop #(.trigger("falling")) j_k_ff_2 (
    .J(j_k_ff_4_qn), .clk(out_4), .K(1'b1), .Q(out_3));  // open: Qn, preset, en, reset
  J_K_Flip_Flop #(.trigger("falling")) j_k_ff_3 (
    .J(1'b1), .clk(out_3), .K(1'b1), .Q(out_2));  // open: Qn, preset, en, reset
  J_K_Flip_Flop #(.trigger("falling")) j_k_ff_4 (
    .J(and_1_out), .clk(out_3), .K(1'b1), .Q(out_1), .Qn(j_k_ff_4_qn));  // open: preset, en, reset
endmodule
