// Logisim project File_3.circ as structural Verilog
module siso (
  input  DIN,
  input  B3,
  input  B2,
  input  B1,
  input  B0,
  input  in_6,
  output out_7,
  output out_8
);

  wire and_1_out, and_2_out, and_3_out, and_4_out, and_5_out, and_6_out, clock_1_out, clock_2_out, d_ff_1_q,
       d_ff_2_q, d_ff_3_q, d_ff_4_q, d_ff_5_q, d_ff_6_q, not_1_out, or_1_out, or_2_out, or_3_out;

  Clock clock_1 (.out(clock_1_out));
  not not_1 (not_1_out, in_6);
  Clock clock_2 (.out(clock_2_out));
  D_Flip_Flop d_ff_1 (.clk(clock_1_out), .D(DIN), .Q(d_ff_1_q));  // open: Qn, preset, en, reset
  D_Flip_Flop d_ff_2 (.clk(clock_2_out), .D(B3), .Q(d_ff_2_q));  // open: Qn, preset, en, reset
  D_Flip_Flop d_ff_3 (.clk(clock_1_out), .D(d_ff_1_q), .Q(d_ff_3_q));  // open: Qn, preset, en, reset
  and and_1 (and_1_out, not_1_out, B2);
  and and_2 (and_2_out, in_6, d_ff_2_q);
  or or_1 (or_1_out, and_2_out, and_1_out);
  and and_3 (and_3_out, in_6, d_ff_4_q);
  D_Flip_Flop d_ff_4 (.clk(clock_2_out), .D(or_1_out), .Q(d_ff_4_q));  // open: Qn, preset, en, reset
  D_Flip_Flop d_ff_5 (.clk(clock_1_out), .D(d_ff_3_q), .Q(d_ff_5_q));  // open: Qn, preset, en, reset
  and and_4 (and_4_out, not_1_out, B1);
  or or_2 (or_2_out, and_3_out, and_4_out);
  D_Flip_Flop d_ff_6 (.clk(clock_2_out), .D(or_2_out), .Q(d_ff_6_q));  // open: Qn, preset, en, reset
  D_Flip_Flop d_ff_7 (.clk(clock_1_out), .D(d_ff_5_q), .Q(out_7));  // open: Qn, preset, en, reset
  and and_5 (and_5_out, in_6, d_ff_6_q);
  or or_3 (or_3_out, and_5_out, and_6_out);
  and and_6 (and_6_out, not_1_out, B0);
  D_Flip_Flop d_ff_8 (.clk(clock_2_out), .D(or_3_out), .Q(out_8));  // open: Qn, preset, en, reset
endmodule
